# Fritzing sketch Badgeuse ESTIAM (saved by Fritzing 0.9.3b)

parts:
  Composant1 = Arduino Uno (Rev3)
  Composant2 = RFID-RC522-v2

nets:
  N1: Composant1.D9_PWM, Composant2.RST
  N2: Composant1.D11_PWM/MOSI, Composant2.MOSI
  N3: Composant1.D12/MISO, Composant2.MISO
  N4: Composant1.D13/SCK, Composant2.SCK
  3V3: Composant1.3V3, Composant2.3.3V
  GND: Composant1.GND, Composant2.GND

custom parts:
  RFID-RC522-v2: A simple China made RFID-RC522 Reader; do check the pin labels, as this is a MFRC522 based clone.
